# Fritzing sketch NovoPainel (saved by Fritzing 0.9.2b)
circuit board: 19cm x 5.64444cm
breadboards: 1

parts:
  J1 = female pin header, 2 pins [form="♀ (female)"]
  J2 = female pin header, 2 pins [form="♀ (female)"]
  S1 = SWITCH-MOMENTARY-2 [package=tactile-switch-1101ne]
  J3 = female pin header, 2 pins [form="♀ (female)"]
  C1 = Electrolytic Capacitor [capacitance=100µF package="200 mil [THT, electrolytic]"]
  S2 = SWITCH-MOMENTARY-2 [package=tactile-switch-1101ne]
  J4 = female pin header, 2 pins [form="♀ (female)"]
  C2 = Electrolytic Capacitor [capacitance=100µF package="200 mil [THT, electrolytic]"]
  U1 = Voltage Regulator [package=to220-adj]
  R1 = Resistor [tolerance=±5% resistance=220 package=THT]
  R2 = Resistor [tolerance=±5% resistance=220 package=THT]
  C3 = Electrolytic Capacitor [capacitance=100µF package="200 mil [THT, electrolytic]"]
  J5 = female pin header, 2 pins [form="♀ (female)"]

nets:
  N1: J1.pin1, J2.pin1, S1.1
  N2: J1.pin2, J2.pin2, J3.pin2, C1.-, J4.pin2, C2.-, R2.Pin_1, C3.-, J5.pin2
  N3: S1.2, J3.pin1, C1.+, S2.1, C2.+, U1.IN
  N4: S2.2, J4.pin1
  N5: U1.ADJ, R1.Pin_1, R2.Pin_0
  Aqui comeca alimentacao de outras partes: U1.OUT, R1.Pin_0, C3.+, J5.pin1

notes:
  +
  -
  B1
  B2
  V1
  S1
  Baterias em paralelo
  Verificar tamanho do borne para ajustar na pcb
  Switch geral do robo
  voltímetro
  switch dos motores
  saída dos motores
  Capacitor alto
  regulador ajustável
  Aqui comeca a alimentacao dos outros componentes
  Voltimetro
  Pensar onde o arduino vai ser alimentado
